// Logisim project JK_Moore_LAB2.circ as structural Verilog: 2 circuits, main circuit maquina
// Maquina de estados
module maquina (
  input  D,
  input  CLK,
  input  CLEAR,
  output [3:0] out_4,
  output S1,
  output S2,
  output S3,
  output S4
);

  wire and_1_out, and_2_out, and_3_out, and_4_out, and_5_out, and_6_out, and_7_out, and_8_out, and_9_out,
       and_10_out, and_11_out, and_12_out, and_13_out, and_14_out, and_15_out, and_16_out, and_17_out,
       and_18_out, and_19_out, and_20_out, and_21_out, and_22_out, and_23_out, and_24_out, and_25_out,
       and_26_out, and_27_out, and_28_out, and_29_out, and_31_out, and_32_out, J0, J1, J2, J3, K0, K1, K2,
       K3, not_1_out, not_2_out, not_3_out, not_4_out, not_5_out, or_1_out, or_2_out, or_3_out, or_4_out,
       or_5_out, or_6_out, or_7_out, or_8_out, or_9_out, or_10_out, or_11_out, or_18_out, or_19_out;

  not not_1 (not_1_out, out_4[3]);
  not not_2 (not_2_out, out_4[1]);
  not not_3 (not_3_out, D);
  not not_4 (not_4_out, out_4[0]);
  not not_5 (not_5_out, out_4[2]);
  and and_1 (and_1_out, not_1_out, out_4[2], out_4[1], D);
  and and_2 (and_2_out, not_1_out, out_4[2], out_4[0], D);
  and and_3 (and_3_out, not_2_out, not_3_out);
  and and_4 (and_4_out, not_4_out, not_3_out);
  and and_5 (and_5_out, out_4[2], not_2_out, out_4[0]);
  and and_6 (and_6_out, not_1_out, out_4[1]);
  and and_7 (and_7_out, out_4[3], not_5_out, not_3_out);
  and and_8 (and_8_out, out_4[3], not_2_out, out_4[0]);
  and and_9 (and_9_out, not_1_out, not_4_out, not_3_out);
  and and_10 (and_10_out, not_1_out, out_4[0], D);
  and and_11 (and_11_out, out_4[1], not_4_out, D);
  and and_12 (and_12_out, out_4[3], not_2_out, out_4[0], not_3_out);
  and and_13 (and_13_out, not_4_out, D);
  and and_14 (and_14_out, not_1_out, not_5_out, D);
  and and_15 (and_15_out, out_4[3], out_4[2], not_2_out, D);
  and and_16 (and_16_out, out_4[3], not_5_out, out_4[0], not_3_out);
  and and_17 (and_17_out, not_1_out, not_4_out);
  and and_18 (and_18_out, not_5_out, not_4_out);
  and and_19 (and_19_out, not_4_out, not_3_out);
  and and_20 (and_20_out, not_1_out, not_5_out, D);
  and and_21 (and_21_out, out_4[3], not_5_out, not_3_out);
  and and_22 (and_22_out, not_1_out, out_4[2]);
  and and_23 (and_23_out, not_1_out, not_2_out, not_3_out);
  and and_24 (and_24_out, not_1_out, out_4[1], D);
  and and_25 (and_25_out, out_4[2], out_4[1], not_4_out, D);
  and and_26 (and_26_out, out_4[3], not_5_out, not_2_out, D);
  and and_27 (and_27_out, not_1_out, out_4[2]);
  and and_28 (and_28_out, not_1_out, out_4[1], not_3_out);
  and and_29 (and_29_out, out_4[3], not_5_out, not_2_out);
  and and_30 (S1, not_1_out, out_4[2], out_4[1], not_4_out);
  and and_31 (and_31_out, out_4[3], not_5_out, out_4[1], not_4_out);
  and and_32 (and_32_out, out_4[3], out_4[2], not_2_out, not_4_out);
  and and_33 (S3, out_4[3], out_4[2], not_2_out, out_4[0]);
  and and_34 (S4, out_4[3], out_4[2], out_4[1], not_4_out);
  or or_1 (or_1_out, and_3_out, and_4_out);
  or or_2 (or_2_out, and_6_out, and_7_out);
  or or_3 (or_3_out, and_9_out, and_10_out);
  or or_4 (or_4_out, and_11_out, and_12_out);
  or or_5 (or_5_out, and_13_out, and_14_out);
  or or_6 (or_6_out, and_15_out, and_16_out);
  or or_7 (or_7_out, and_17_out, and_18_out);
  or or_8 (or_8_out, and_19_out, and_20_out);
  or or_9 (or_9_out, and_22_out, and_23_out);
  or or_10 (or_10_out, and_24_out, and_25_out);
  or or_11 (or_11_out, and_27_out, and_28_out);
  or or_12 (S2, and_31_out, and_32_out);
  or or_13 (J3, and_1_out, and_2_out);
  or or_14 (K3, or_1_out, and_5_out);
  or or_15 (J2, or_2_out, and_8_out);
  or or_16 (K2, or_3_out, or_4_out);
  or or_17 (J1, or_5_out, or_6_out);
  or or_18 (or_18_out, or_7_out, or_8_out);
  or or_19 (or_19_out, or_9_out, or_10_out);
  or or_20 (K0, or_11_out, and_29_out);
  or or_21 (K1, or_18_out, and_21_out);
  or or_22 (J0, or_19_out, and_26_out);
  J_K_Flip_Flop FF3 (.J(J3), .clk(CLK), .K(K3), .Q(out_4[3]), .reset(CLEAR));  // open: Qn, preset, en
  J_K_Flip_Flop FF2 (.J(J2), .clk(CLK), .K(K2), .Q(out_4[2]), .reset(CLEAR));  // open: Qn, preset, en
  J_K_Flip_Flop FF1 (.J(J1), .clk(CLK), .K(K1), .Q(out_4[1]), .reset(CLEAR));  // open: Qn, preset, en
  J_K_Flip_Flop FF0 (.J(J0), .clk(CLK), .K(K0), .Q(out_4[0]), .reset(CLEAR));  // open: Qn, preset, en

  // Other names for the same wires on the sheet: Q0 = out_4[0]; Q1 = out_4[1]; Q2 = out_4[2]; Q3 = out_4[3]
endmodule

module main (
  input  D,
  input  Clock,
  input  Reset
);

  wire maquina_1_s1, maquina_1_s2, maquina_1_s3, maquina_1_s4, visualizador_1_a0, visualizador_1_a1,
       visualizador_1_b0, visualizador_1_b1, visualizador_1_c0, visualizador_1_c1, visualizador_1_d0,
       visualizador_1_d1, visualizador_1_e0, visualizador_1_e1, visualizador_1_f0, visualizador_1_f1,
       visualizador_1_g0, visualizador_1_g1, visualizador_1_s1_2, visualizador_1_s2_2, visualizador_1_s3_2,
       visualizador_1_s4_2;
  wire [3:0] maquina_1_out_4;

  maquina maquina_1 (
    .D(D), .CLK(Clock), .CLEAR(Reset), .S1(maquina_1_s1), .S2(maquina_1_s2), .S3(maquina_1_s3),
    .S4(maquina_1_s4), .out_4(maquina_1_out_4));
  Visualizador visualizador_1 (
    .Estado_Actual(maquina_1_out_4), .S1(maquina_1_s1), .S2(maquina_1_s2), .S3(maquina_1_s3),
    .S4(maquina_1_s4), .a0(visualizador_1_a0), .b0(visualizador_1_b0), .c0(visualizador_1_c0),
    .d0(visualizador_1_d0), .e0(visualizador_1_e0), .f0(visualizador_1_f0), .g0(visualizador_1_g0),
    .a1(visualizador_1_a1), .b1(visualizador_1_b1), .c1(visualizador_1_c1), .d1(visualizador_1_d1),
    .e1(visualizador_1_e1), .f1(visualizador_1_f1), .g1(visualizador_1_g1), .S1_2(visualizador_1_s1_2),
    .S2_2(visualizador_1_s2_2), .S3_2(visualizador_1_s3_2), .S4_2(visualizador_1_s4_2));
  LED led_1 (.in(visualizador_1_s2_2));
  LED led_2 (.in(visualizador_1_s1_2));
  LED led_3 (.in(visualizador_1_s3_2));
  LED led_4 (.in(visualizador_1_s4_2));
  _7_Segment_Display u_7_segment_display_1 (
    .g(visualizador_1_g0), .f(visualizador_1_f0), .a(visualizador_1_a0), .b(visualizador_1_b0),
    .e(visualizador_1_e0), .d(visualizador_1_d0), .c(visualizador_1_c0));  // open: dp
  _7_Segment_Display u_7_segment_display_2 (
    .g(visualizador_1_g1), .f(visualizador_1_f1), .a(visualizador_1_a1), .b(visualizador_1_b1),
    .e(visualizador_1_e1), .d(visualizador_1_d1), .c(visualizador_1_c1));  // open: dp
endmodule
