// Logisim project divisor.circ as structural Verilog: 4 circuits, main circuit main
module main (
  input  [3:0] in_1,
  input  in_2,
  input  in_3,
  input  in_4,
  input  in_5
);

  wire visualizador_1_a0, visualizador_1_a1, visualizador_1_b0, visualizador_1_b1, visualizador_1_c0,
       visualizador_1_c1, visualizador_1_d0, visualizador_1_d1, visualizador_1_e0, visualizador_1_e1,
       visualizador_1_f0, visualizador_1_f1, visualizador_1_g0, visualizador_1_g1, visualizador_1_s1_2,
       visualizador_1_s2_2, visualizador_1_s3_2, visualizador_1_s4_2;

  Visualizador visualizador_1 (
    .Estado_Actual(in_1), .S1(in_2), .S2(in_3), .S3(in_4), .S4(in_5), .a0(visualizador_1_a0),
    .b0(visualizador_1_b0), .c0(visualizador_1_c0), .d0(visualizador_1_d0), .e0(visualizador_1_e0),
    .f0(visualizador_1_f0), .g0(visualizador_1_g0), .a1(visualizador_1_a1), .b1(visualizador_1_b1),
    .c1(visualizador_1_c1), .d1(visualizador_1_d1), .e1(visualizador_1_e1), .f1(visualizador_1_f1),
    .g1(visualizador_1_g1), .S1_2(visualizador_1_s1_2), .S2_2(visualizador_1_s2_2),
    .S3_2(visualizador_1_s3_2), .S4_2(visualizador_1_s4_2));
  LED led_1 (.in(visualizador_1_s1_2));
  LED led_2 (.in(visualizador_1_s3_2));
  LED led_3 (.in(visualizador_1_s2_2));
  LED led_4 (.in(visualizador_1_s4_2));
  _7_Segment_Display u_7_segment_display_1 (
    .g(visualizador_1_g0), .f(visualizador_1_f0), .a(visualizador_1_a0), .b(visualizador_1_b0),
    .e(visualizador_1_e0), .d(visualizador_1_d0), .c(visualizador_1_c0));  // open: dp
  _7_Segment_Display u_7_segment_display_2 (
    .g(visualizador_1_g1), .f(visualizador_1_f1), .a(visualizador_1_a1), .b(visualizador_1_b1),
    .e(visualizador_1_e1), .d(visualizador_1_d1), .c(visualizador_1_c1));  // open: dp
endmodule

module BCD (
  input  [3:0] in_1
);

  wire conversor_1_a_2, conversor_1_b_2, conversor_1_c_2, conversor_1_d_2, conversor_1_e, conversor_1_f,
       conversor_1_g, conversor_2_a_2, conversor_2_b_2, conversor_2_c_2, conversor_2_d_2, conversor_2_e,
       conversor_2_f, conversor_2_g;
  wire [3:0] divider_1_out, divider_1_rem;

  Divider #(.width(4)) divider_1 (
    .a(in_1), .b(4'b1010), .out({divider_1_out[3:2], divider_1_out[2], divider_1_out[0]}), .rem(divider_1_rem));  // open: upper
  conversor conversor_1 (
    .D(divider_1_rem[3]), .C(divider_1_rem[2]), .B(divider_1_rem[1]), .A(divider_1_rem[0]),
    .a_2(conversor_1_a_2), .b_2(conversor_1_b_2), .c_2(conversor_1_c_2), .d_2(conversor_1_d_2),
    .e(conversor_1_e), .f(conversor_1_f), .g(conversor_1_g));
  _7_Segment_Display u_7_segment_display_1 (
    .g(conversor_1_g), .f(conversor_1_f), .a(conversor_1_a_2), .b(conversor_1_b_2), .e(conversor_1_e),
    .d(conversor_1_d_2), .c(conversor_1_c_2));  // open: dp
  conversor conversor_2 (
    .D(divider_1_out[3]), .C(divider_1_out[2]), .B(divider_1_out[2]), .A(divider_1_out[0]),
    .a_2(conversor_2_a_2), .b_2(conversor_2_b_2), .c_2(conversor_2_c_2), .d_2(conversor_2_d_2),
    .e(conversor_2_e), .f(conversor_2_f), .g(conversor_2_g));
  _7_Segment_Display u_7_segment_display_2 (
    .g(conversor_2_g), .f(conversor_2_f), .a(conversor_2_a_2), .b(conversor_2_b_2), .e(conversor_2_e),
    .d(conversor_2_d_2), .c(conversor_2_c_2));  // open: dp
endmodule

module conversor (
  input  D,
  input  C,
  input  B,
  input  A,
  output a_2,
  output b_2,
  output c_2,
  output d_2,
  output e,
  output f,
  output g
);

  wire and_1_out, and_2_out, and_3_out, and_4_out, and_5_out, and_6_out, and_7_out, and_8_out, and_9_out,
       and_10_out, and_11_out, and_12_out, and_13_out, and_14_out, and_15_out, and_16_out, not_1_out,
       not_2_out, not_3_out, not_4_out, not_5_out, not_6_out, not_7_out, not_8_out, not_9_out, not_10_out,
       not_11_out, not_12_out, not_13_out, not_14_out, not_15_out, not_16_out, not_17_out, not_18_out,
       not_19_out, not_20_out, not_21_out;

  not not_1 (not_1_out, C);
  and and_1 (and_1_out, not_1_out, not_2_out);
  not not_2 (not_2_out, A);
  and and_2 (and_2_out, C, A);
  not not_3 (not_3_out, C);
  not not_4 (not_4_out, B);
  and and_3 (and_3_out, not_4_out, not_5_out);
  not not_5 (not_5_out, A);
  and and_4 (and_4_out, B, A);
  not not_6 (not_6_out, B);
  or or_1 (c_2, not_6_out, A, C);
  not not_7 (not_7_out, C);
  and and_5 (and_5_out, not_7_out, not_8_out);
  not not_8 (not_8_out, A);
  not not_9 (not_9_out, C);
  and and_6 (and_6_out, not_9_out, B);
  and and_7 (and_7_out, B, not_10_out);
  not not_10 (not_10_out, A);
  and and_8 (and_8_out, C, not_11_out, A);
  not not_11 (not_11_out, B);
  not not_12 (not_12_out, C);
  and and_9 (and_9_out, not_12_out, not_13_out);
  not not_13 (not_13_out, A);
  and and_10 (and_10_out, B, not_14_out);
  not not_14 (not_14_out, A);
  not not_15 (not_15_out, B);
  and and_11 (and_11_out, not_15_out, not_16_out);
  not not_16 (not_16_out, A);
  and and_12 (and_12_out, C, not_17_out);
  not not_17 (not_17_out, B);
  and and_13 (and_13_out, C, not_18_out);
  not not_18 (not_18_out, A);
  not not_19 (not_19_out, C);
  and and_14 (and_14_out, not_19_out, B);
  and and_15 (and_15_out, C, not_20_out);
  not not_20 (not_20_out, B);
  and and_16 (and_16_out, C, not_21_out);
  not not_21 (not_21_out, A);
  or or_2 (a_2, and_1_out, B, and_2_out, D);
  or or_3 (b_2, not_3_out, and_3_out, and_4_out);
  or or_4 (d_2, and_5_out, and_6_out, and_7_out, and_8_out, D);
  or or_5 (e, and_9_out, and_10_out);
  or or_6 (f, and_11_out, and_12_out, and_13_out, D);
  or or_7 (g, and_14_out, and_15_out, and_16_out, D);
endmodule

module Visualizador (
  input  [3:0] Estado_Actual,
  input  S1,
  input  S2,
  input  S3,
  input  S4,
  output a0,
  output b0,
  output c0,
  output d0,
  output e0,
  output f0,
  output g0,
  output a1,
  output b1,
  output c1,
  output d1,
  output e1,
  output f1,
  output g1,
  output S1_2,
  output S2_2,
  output S3_2,
  output S4_2
);

  wire [3:0] divider_1_out, divider_1_rem;

  Divider #(.width(4)) divider_1 (
    .a(Estado_Actual), .b(4'b1010), .out({divider_1_out[3:2], divider_1_out[2], divider_1_out[0]}),
    .rem(divider_1_rem));  // open: upper
  conversor conversor_1 (
    .D(divider_1_rem[3]), .C(divider_1_rem[2]), .B(divider_1_rem[1]), .A(divider_1_rem[0]), .a_2(a1),
    .b_2(b1), .c_2(c1), .d_2(d1), .e(e1), .f(f1), .g(g1));
  conversor conversor_2 (
    .D(divider_1_out[3]), .C(divider_1_out[2]), .B(divider_1_out[2]), .A(divider_1_out[0]), .a_2(a0),
    .b_2(b0), .c_2(c0), .d_2(d0), .e(e0), .f(f0), .g(g0));

  assign S1_2 = S1;
  assign S2_2 = S2;
  assign S3_2 = S3;
  assign S4_2 = S4;
endmodule
